# Fritzing sketch Dendrometer (saved by Fritzing 0.8.7b)
breadboards: 1

parts:
  Part1 = Adafruit Feather M0 RFM9x LoRa [part_number="Adafruit #3178 or #3179"]
  S1 = Square Pushbutton
  Part2 = Adafruit Breadboard-Friendly NeoPixel [part_number="Adafruit #1312"]
  U1 = SHT1x Humdity Sensor [package=sht1x]

nets:
  N1: Part1.A2, Part2.IN
  GND: Part1.GND, S1.leg0, Part2.GND, U1.GND
  N2: Part1.D10, S1.leg1
  N3: Part1.SCL, U1.SCK
  N4: Part1.SDA, U1.DATA
  5V: Part2.VDD, U1.VDD

notes:
  5V goes to Hypnos Rail

custom parts:
  Adafruit Feather M0 RFM9x LoRa: This is the Adafruit Feather M0 RFM95 LoRa Radio - our take on an microcontroller with a "Long Range (LoRa)" packet radio transceiver with built in USB and battery charging. Its an Adafruit Feather M0 with a 433Mhz or 900MHz radio module cooked in! Great for making wireless networks that are more flexible than Bluetooth LE and without the high power requirements of WiFi. We have other boards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
  Adafruit Breadboard-Friendly NeoPixel: This is the easiest way possible to add small, bright RGB pixels to your project. We took the same technology from our Flora NeoPixels and made them breadboard friendly, with two rows of 3 x 0.1" spaced header on each side for easy soldering, chaining and breadboarding. These ultra-bright LEDs have a constant-current driver cooked right into the LED package! The pixels are chainable - so you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
